// Logisim project 1_CIRCUIT.circ as structural Verilog: 1 circuit, main circuit main
module main (
  input  SW_0,
  input  SW_1,
  input  SW_2,
  output LED_0,
  output LED_1,
  output LED_2
);

  and and_1 (LED_0, SW_0, SW_1);
  or or_1 (LED_2, LED_0, SW_2);

  assign LED_1 = LED_0;
endmodule
